# Fritzing sketch KIT_CIBERSEGURIDAD (saved by Fritzing 1.0.7)
circuit board: 8.46667cm x 5.64444cm

parts:
  A1 = ESP32-S3 Wroom board Freenove
  A2 = Freenove ESP32 breakout board
  Motor_Derecho = gear-motor
  Motor_Izquierdo = gear-motor
  Driver_TB6612FNG = Motor Driver 1A Dual TB6612FNG
  HC-SR04_Sensor_Ultrasonido = HC-SR04 Ultrasonic Distance Sensor
  OLED_I2C_128x64 = OLED 128x64 I2C Monochrome Display
  WS2812_NeoPIXEL = Adafruit Pixie [part_number="Adafruit #2741"]
  S1 = Round Pushbutton
  JACK1 = 2.1mm Barrel Jack with Terminal Block
  18650 = 18650 battery holder [package=battery-18650-kit]
  18650_2 = 18650 battery holder [package=battery-18650-kit]
  BMS_2S_8A = 2S-BMS

nets:
  N1: A1.Pin_1, A2.Pin_21, A2.Pin_81, Driver_TB6612FNG.VCC
  N2: A1.Pin_2, A2.Pin_22, A2.Pin_82
  N3: A1.Pin_3, A2.Pin_23, A2.Pin_83
  N4: A1.Pin_4, A2.Pin_24, A2.Pin_84
  N5: A1.Pin_5, A2.Pin_5, A2.Pin_85
  N6: A1.Pin_6, A2.Pin_26, A2.Pin_86
  N7: A1.Pin_7, A2.Pin_27, A2.Pin_87
  N8: A1.Pin_8, A2.Pin_8, A2.Pin_88
  N9: A1.Pin_9, A2.Pin_29, A2.Pin_89
  N10: A1.Pin_10, A2.Pin_30, A2.Pin_90
  N11: A1.Pin_11, A2.Pin_31, A2.Pin_91
  N12: A1.Pin_12, A2.Pin_32, A2.Pin_92, HC-SR04_Sensor_Ultrasonido.TRIG
  N13: A1.Pin_13, A2.Pin_33, A2.Pin_93
  N14: A1.Pin_14, A2.Pin_34, A2.Pin_94
  N15: A1.Pin_15, A2.Pin_15, A2.Pin_95
  N16: A1.Pin_16, A2.Pin_36, A2.Pin_96
  N17: A1.Pin_17, A2.Pin_97
  N18: A1.Pin_18, A2.Pin_98
  N19: A1.Pin_19, A2.Pin_39, A2.Pin_99, HC-SR04_Sensor_Ultrasonido.ECHO
  N20: A1.Pin_20, A2.Pin_100
  N21: A1.Pin_21, A2.Pin_117, A2.Pin_197
  N22: A1.Pin_22, A2.Pin_118, A2.Pin_198
  N23: A1.Pin_23, A2.Pin_119
  N24: A1.Pin_24, A2.Pin_120, A2.Pin_180, Driver_TB6612FNG.STBY
  N25: A1.Pin_25, A2.Pin_121, A2.Pin_181, Driver_TB6612FNG.AIN2
  N26: A1.Pin_26, A2.Pin_122, A2.Pin_182, WS2812_NeoPIXEL.IN
  N27: A1.Pin_27, A2.Pin_123
  N28: A1.Pin_28, A2.Pin_124, A2.Pin_204
  N29: A1.Pin_29, A2.Pin_125, A2.Pin_205
  N30: A1.Pin_30, A2.Pin_126
  N31: A1.Pin_31, A2.Pin_127
  N32: A1.Pin_32, A2.Pin_128, A2.Pin_188, OLED_I2C_128x64.SDA
  N33: A1.Pin_33, A2.Pin_129, A2.Pin_189, Driver_TB6612FNG.PWMA
  N34: A1.Pin_34, A2.Pin_130, A2.Pin_190, A2.Pin_210, Driver_TB6612FNG.AIN1
  N35: A1.Pin_35, A2.Pin_131, A2.Pin_191, Driver_TB6612FNG.PWMB
  N36: A1.Pin_36, A2.Pin_132, A2.Pin_192, Driver_TB6612FNG.BIN1
  N37: A1.Pin_37, A2.Pin_133, A2.Pin_193, Driver_TB6612FNG.BIN2
  N38: A1.Pin_38, A2.Pin_134, A2.Pin_194, OLED_I2C_128x64.SCK
  N39: A1.Pin_39, A2.Pin_135, A2.Pin_215
  N40: A1.Pin_40, A2.Pin_136
  GND: A2.Pin_61, A2.Pin_62, A2.Pin_101, A2.Pin_105, A2.Pin_108, A2.Pin_141, A2.Pin_156, Driver_TB6612FNG.GND, HC-SR04_Sensor_Ultrasonido.GND, OLED_I2C_128x64.GND, WS2812_NeoPIXEL.GND
  VCC: A2.Pin_112, A2.Pin_115, A2.Pin_116, HC-SR04_Sensor_Ultrasonido.VCC, OLED_I2C_128x64.VDD, WS2812_NeoPIXEL.5V
  N41: Motor_Derecho.pin_1, Driver_TB6612FNG.A01
  N42: Motor_Derecho.pin_2, Driver_TB6612FNG.A02
  N43: Motor_Izquierdo.pin_1, Driver_TB6612FNG.B01
  N44: Motor_Izquierdo.pin_2, Driver_TB6612FNG.B02
  N45: Driver_TB6612FNG.VM, S1.leg0, JACK1.NEG
  N46: S1.leg1, 18650.-, BMS_2S_8A.pin1
  N47: JACK1.POS, 18650_2.+, BMS_2S_8A.pin2
  N48: 18650.+, 18650_2.-, BMS_2S_8A.pin3

custom parts:
  ESP32-S3 Wroom board Freenove: ESP32-S3-WROOM is a powerful and small controller with onboard wireless and camera.
  Freenove ESP32 breakout board: This breakout board can help you wire and know the status of the GPIO.
  18650 battery holder: 18650 Battery
  2S-BMS: 2S-BMS LIPO battery charger / protection unit. Note pcb does not match the board as it will likely connect with wires, so pcb is 5 pads suitable for .1in header pins.
